# Fritzing sketch DFW-InfoSec-Badge-2018 (saved by Fritzing 0.9.3b)
circuit board: 6.99912cm x 23.4809cm
breadboards: 1

parts:
  Part1 = Arduino Nano (Rev3.0)
  R3 = Resistor [tolerance=±5% resistance=150 package=THT]
  R2 = Resistor [tolerance=±5% resistance=150 package=THT]
  R1 = Resistor [tolerance=±5% resistance=150 package=THT]
  R7 = Resistor [tolerance=±5% resistance=150 package=THT]
  R8 = Resistor [tolerance=±5% resistance=150 package=THT]
  R9 = Resistor [tolerance=±5% resistance=150 package=THT]
  R10 = Resistor [tolerance=±5% resistance=150 package=THT]
  R11 = Resistor [tolerance=±5% resistance=150 package=THT]
  R12 = Resistor [tolerance=±5% resistance=150 package=THT]
  R15 = Resistor [tolerance=±5% resistance=150 package=THT]
  R14 = Resistor [tolerance=±5% resistance=150 package=THT]
  R4 = Resistor [tolerance=±5% resistance=150 package=THT]
  R5 = Resistor [tolerance=±5% resistance=150 package=THT]
  R6 = Resistor [tolerance=±5% resistance=150 package=THT]
  R13 = Resistor [tolerance=±5% resistance=150 package=THT]
  J3 = female pin header, 4 pins [form="♀ (female)"]
  J2 = female pin header, 4 pins [form="♀ (female)"]
  J4 = female pin header, 5 pins [form="♀ (female)"]
  LED4 = RGB LED (com. cathode, rbg) [package="5 mm [THT]"]
  LED3 = RGB LED (com. cathode, rbg) [package="5 mm [THT]"]
  LED1 = RGB LED (com. cathode, rbg) [package="5 mm [THT]"]
  LED2 = RGB LED (com. cathode, rbg) [package="5 mm [THT]"]
  LED5 = RGB LED (com. cathode, rbg) [package="5 mm [THT]"]
  VCC1 = Battery block 9V

nets:
  N1: Part1.D1/TX, J2.pin1
  N2: Part1.D0/RX, J2.pin2
  N3: Part1.RESET, J2.pin3, J4.pin1
  N4: Part1.GND, J2.pin4, LED4.common_cathode, LED3.common_cathode, LED1.common_cathode, LED2.common_cathode, LED5.common_cathode, VCC1.-
  N5: Part1.D2, R3.Pin_1
  N6: Part1.D3, R2.Pin_1
  N7: Part1.D4, R1.Pin_1
  N8: Part1.D5, R7.Pin_1
  N9: Part1.D6, R8.Pin_1
  N10: Part1.D7, R9.Pin_1
  N11: Part1.D8, R10.Pin_1
  N12: Part1.D9, R11.Pin_1
  N13: Part1.D10, R12.Pin_1
  N14: Part1.D11/MOSI, R15.Pin_1
  N15: Part1.D12/MISO, R14.Pin_1
  N16: Part1.VIN, VCC1.+
  N17: Part1.5V, J4.pin2
  N18: Part1.A7, J4.pin3
  N19: Part1.A6, J4.pin4
  N20: Part1.A5, J4.pin5
  N21: Part1.A4, R4.Pin_1
  N22: Part1.A3, R5.Pin_1
  N23: Part1.A2, R6.Pin_1
  N24: Part1.A1, R13.Pin_1
  N25: Part1.A0, J3.pin1
  N26: Part1.AREF, J3.pin2
  N27: Part1.3V3, J3.pin3
  N28: Part1.D13/SCK, J3.pin4
  N29: R3.Pin_0, LED1.red_anode
  N30: R2.Pin_0, LED1.blue_anode
  N31: R1.Pin_0, LED1.green_anode
  N32: R7.Pin_0, LED3.red_anode
  N33: R8.Pin_0, LED3.blue_anode
  N34: R9.Pin_0, LED3.green_anode
  N35: R10.Pin_0, LED4.red_anode
  N36: R11.Pin_0, LED4.blue_anode
  N37: R12.Pin_0, LED4.green_anode
  N38: R15.Pin_0, LED5.green_anode
  N39: R14.Pin_0, LED5.blue_anode
  N40: R4.Pin_0, LED2.red_anode
  N41: R5.Pin_0, LED2.blue_anode
  N42: R6.Pin_0, LED2.green_anode
  N43: R13.Pin_0, LED5.red_anode

notes:
  +VIN
  -GND

// code stored in the sketch: DFW-InfoSec-Badge-RGB_LED_TEST.ino
// Define Pins
#define LED1_RED 2
#define LED1_GREEN 4
#define LED1_BLUE 3

#define LED2_RED 5
#define LED2_GREEN 7
#define LED2_BLUE 6

#define LED3_RED 8
#define LED3_GREEN 10
#define LED3_BLUE 9

#define LED4_RED A4
#define LED4_GREEN A2
#define LED4_BLUE A3

#define LED5_RED A1
#define LED5_GREEN 11
#define LED5_BLUE 12


void setup()
{
  // Initialize Pins As Output
  pinMode(LED1_RED, OUTPUT);
  pinMode(LED1_GREEN, OUTPUT);
  pinMode(LED1_BLUE, OUTPUT);
  pinMode(LED2_RED, OUTPUT);
  pinMode(LED2_GREEN, OUTPUT);
  pinMode(LED2_BLUE, OUTPUT);
  pinMode(LED3_RED, OUTPUT);
  pinMode(LED3_GREEN, OUTPUT);
  pinMode(LED3_BLUE, OUTPUT);
  pinMode(LED4_RED, OUTPUT);
  pinMode(LED4_GREEN, OUTPUT);
  pinMode(LED4_BLUE, OUTPUT);
  pinMode(LED5_RED, OUTPUT);
  pinMode(LED5_GREEN, OUTPUT);
  pinMode(LED5_BLUE, OUTPUT);
}

// Main Loop
void loop()
{
  
  // New Code Work for Digital HIGH/LOW
  int DelayTime = 250;
  // RED
  digitalWrite(LED1_RED, HIGH);
  digitalWrite(LED2_RED, HIGH);
  digitalWrite(LED3_RED, HIGH);
  digitalWrite(LED4_RED, HIGH);
  digitalWrite(LED5_RED, HIGH);
  delay(DelayTime);
  // RED + GREEN
  digitalWrite(LED1_GREEN, HIGH);
  digitalWrite(LED2_GREEN, HIGH);
  digitalWrite(LED3_GREEN, HIGH);
  digitalWrite(LED4_GREEN, HIGH);
  digitalWrite(LED5_GREEN, HIGH);
  delay(DelayTime);
  // GREEN
  digitalWrite(LED1_RED, LOW);
  digitalWrite(LED2_RED, LOW);
  digitalWrite(LED3_RED, LOW);
  digitalWrite(LED4_RED, LOW);
  digitalWrite(LED5_RED, LOW);
  delay(DelayTime);
  // GREEN + BLUE
  digitalWrite(LED1_BLUE, HIGH);
  digitalWrite(LED2_BLUE, HIGH);
  digitalWrite(LED3_BLUE, HIGH);
  digitalWrite(LED4_BLUE, HIGH);
  digitalWrite(LED5_BLUE, HIGH);
  delay(DelayTime);
  // BLUE
  digitalWrite(LED1_GREEN, LOW);
  digitalWrite(LED2_GREEN, LOW);
  digitalWrite(LED3_GREEN, LOW);
  digitalWrite(LED4_GREEN, LOW);
  digitalWrite(LED5_GREEN, LOW);
  delay(DelayTime);
  // BLUE + RED
  digitalWrite(LED1_RED, HIGH);
  digitalWrite(LED2_RED, HIGH);
  digitalWrite(LED3_RED, HIGH);
  digitalWrite(LED4_RED, HIGH);
  digitalWrite(LED5_RED, HIGH);
  delay(DelayTime);
  // RBG WHITE
  digitalWrite(LED1_GREEN, HIGH);
  digitalWrite(LED2_GREEN, HIGH);
  digitalWrite(LED3_GREEN, HIGH);
  digitalWrite(LED4_GREEN, HIGH);
  digitalWrite(LED5_GREEN, HIGH);
  delay(DelayTime);
  // ALL OFF NO DELAY
  digitalWrite(LED1_RED, LOW);
  digitalWrite(LED2_RED, LOW);
  digitalWrite(LED3_RED, LOW);
  digitalWrite(LED4_RED, LOW);
  digitalWrite(LED5_RED, LOW);
  digitalWrite(LED1_GREEN, LOW);
  digitalWrite(LED2_GREEN, LOW);
  digitalWrite(LED3_GREEN, LOW);
  digitalWrite(LED4_GREEN, LOW);
  digitalWrite(LED5_GREEN, LOW);
  digitalWrite(LED1_BLUE, LOW);
  digitalWrite(LED2_BLUE, LOW);
  digitalWrite(LED3_BLUE, LOW);
  digitalWrite(LED4_BLUE, LOW);
  digitalWrite(LED5_BLUE, LOW);
  
}
